// Logisim project ALU.circ as structural Verilog: 1 circuit, main circuit main
module main (
  input  [3:0] A,
  input  [3:0] B,
  input  Cin,
  input  [2:0] in_4,
  output [3:0] O,
  output Cout
);

  wire [3:0] adder_1_out, and_1_out, nor_1_out, or_1_out, xor_1_out;

  assign and_1_out = A & B;  // AND_Gate and_1, 4 bits wide
  assign or_1_out = A | B;  // OR_Gate or_1, 4 bits wide
  assign xor_1_out = A ^ B;  // XOR_Gate xor_1, 4 bits wide
  assign nor_1_out = ~(A | B);  // NOR_Gate nor_1, 4 bits wide
  Adder #(.width(4)) adder_1 (.a(A), .b(B), .out(adder_1_out), .cin(Cin), .cout(Cout));
  Hex_Digit_Display hex_digit_display_1 (.value(B));  // open: dp
  Hex_Digit_Display hex_digit_display_2 (.value(A));  // open: dp
  Multiplexer #(.select(3), .width(4), .enable("false")) multiplexer_1 (
    .in0(and_1_out), .in1(or_1_out), .in2(xor_1_out), .in3(nor_1_out), .in4(adder_1_out), .out(O), .sel(in_4));  // open: in5, in6, in7
  Hex_Digit_Display hex_digit_display_3 (.value(O));  // open: dp

  // Notes on the sheet:
  //   Instruction Code
  //   000
  //   001
  //   010
  //   011
  //   100
  //   Open RISC Class I ALU
  //   Instructions 
  //   AND
  //   OR
  //   XOR
  //   NOR
  //   ADD
endmodule
